// Logisim project l5.circ as structural Verilog: 2 circuits, main circuit main
module main (
  input  A4,
  input  A3,
  input  A2,
  input  A1,
  input  B4,
  input  B3,
  input  B2,
  input  B1,
  input  cin_0,
  input  in_10,
  input  in_11,
  output Cout,
  output IGNORE,
  output S3,
  output S2,
  output S1,
  output out_17
);

  wire and_1_out, and_2_out, n74283_2_cout, n74283_2_s1, n74283_2_s2, n74283_2_s3, n74283_2_s4, or_2_out;

  or or_1 (Cout, n74283_2_cout, or_2_out);
  or or_2 (or_2_out, and_1_out, and_2_out);
  and and_1 (and_1_out, n74283_2_s4, n74283_2_s3);
  and and_2 (and_2_out, n74283_2_s4, n74283_2_s2);
  _74283 u_74283_1 (
    .A1(in_10), .B1(n74283_2_s1), .A2(Cout), .B2(n74283_2_s2), .A3(Cout), .B3(n74283_2_s3), .A4(in_10),
    .B4(n74283_2_s4), .cout(IGNORE), .in_1(in_11), .s1(out_17), .s2(S1), .s3(S2), .s4(S3));
  _74283 u_74283_2 (
    .A1(A1), .B1(B1), .A2(A2), .B2(B2), .A3(A3), .B3(B3), .A4(A4), .B4(B4), .cout(n74283_2_cout),
    .in_1(cin_0), .s1(n74283_2_s1), .s2(n74283_2_s2), .s3(n74283_2_s3), .s4(n74283_2_s4));

  // Notes on the sheet:
  //   COUT
  //   S4
  //   S4
  //   S3
  //   B3
  //   B4
  //   S2
  //   S1
  //   B1
  //   B2
endmodule

module _74283 (
  input  in_1,
  input  A1,
  input  B1,
  input  A2,
  input  B2,
  input  A3,
  input  B3,
  input  A4,
  input  B4,
  output s1,
  output s2,
  output s3,
  output s4,
  output cout
);

  wire adder_1_cout, adder_2_cout, adder_3_cout;

  Adder #(.width(1)) adder_1 (.a(A1), .b(B1), .out(s1), .cin(in_1), .cout(adder_1_cout));
  Adder #(.width(1)) adder_2 (.a(A2), .b(B2), .out(s2), .cin(adder_1_cout), .cout(adder_2_cout));
  Adder #(.width(1)) adder_3 (.a(A3), .b(B3), .out(s3), .cin(adder_2_cout), .cout(adder_3_cout));
  Adder #(.width(1)) adder_4 (.a(A4), .b(B4), .out(s4), .cin(adder_3_cout), .cout(cout));
endmodule
