// Logisim project F(A, B, C, D) = Σ (0, 1, 3, 5, 8, 9, 14, 15).circ as structural Verilog: 1 circuit, main circuit main
module main (
  input  in_1,
  input  [3:0] in_2,
  output out_3
);

  Multiplexer #(.select(4), .enable("false")) multiplexer_1 (
    .in0(1'b1), .in1(1'b1), .in2(in_1), .in3(1'b1), .in4(in_1), .in5(1'b1), .in6(in_1), .in7(in_1),
    .in8(1'b1), .in9(1'b1), .in10(in_1), .in11(in_1), .in12(in_1), .in13(in_1), .in14(1'b1), .in15(1'b1),
    .out(out_3), .sel(in_2));

  // Notes on the sheet:
  //   F = minterm(0,1,3,5,8,9,14,15)
endmodule
