// Logisim project lab7 (1).circ as structural Verilog: 1 circuit, main circuit main
module main (
  input  in_1,
  input  [2:0] in_2,
  output out_3
);

  Multiplexer #(.select(3), .enable("false")) multiplexer_1 (
    .in0(1'b1), .in1(1'b1), .in2(in_1), .in3(in_1), .in4(in_1), .in5(1'b1), .in6(in_1), .in7(1'b1),
    .out(out_3), .sel(in_2));
endmodule
