// Logisim project lab7 (2).circ as structural Verilog: 1 circuit, main circuit main
module main (
  input  E,
  input  Io,
  input  I1,
  input  I2,
  input  I3,
  input  S1,
  input  S2,
  output out_8
);

  wire and_1_out, and_2_out, and_3_out, and_4_out, not_1_out, not_2_out, or_1_out, or_2_out;

  not not_1 (not_1_out, S1);
  not not_2 (not_2_out, S2);
  and and_1 (and_1_out, Io, not_1_out, not_2_out, E);
  and and_2 (and_2_out, I1, not_1_out, S2, E);
  and and_3 (and_3_out, I2, S1, not_2_out, E);
  and and_4 (and_4_out, I3, S1, S2, E);
  or or_1 (or_1_out, and_1_out, and_2_out);
  or or_2 (or_2_out, and_3_out, and_4_out);
  or or_3 (out_8, or_1_out, or_2_out);
endmodule
