// Logisim project assignment1.circ as structural Verilog
module main (
  input  in_1,
  input  sensor,
  input  sensor_2,
  input  sensor_3
);

  wire colling_system_1_out_3, compartment_1_out_2, compartment_2_out_2, compartment_3_out_2, not_1_out,
       xor_circuit_with_3_input_1_out_4;

  compartment compartment_1 (.in_1(sensor), .out_2(compartment_1_out_2));
  not not_1 (not_1_out, in_1);
  not_in_circuits_part_just_trail not_in_circuits_part_just_trail_1 ();
  xor_circuit_with_3_input xor_circuit_with_3_input_1 (
    .in_1(compartment_1_out_2), .in_2(compartment_3_out_2), .in_3(compartment_2_out_2),
    .out_4(xor_circuit_with_3_input_1_out_4));
  compartment compartment_2 (.in_1(sensor_2), .out_2(compartment_2_out_2));
  colling_system colling_system_1 (
    .in_1(not_1_out), .in_2(xor_circuit_with_3_input_1_out_4), .out_3(colling_system_1_out_3));
  LED led_1 (.in(colling_system_1_out_3));
  compartment compartment_3 (.in_1(sensor_3), .out_2(compartment_3_out_2));

  // Notes on the sheet:
  //   0 means raise threshold value
  //   0 means cooling systen not working
  //   compartment 1
  //   compartment 2
  //   Alarm signal
  //   compartment 3
endmodule

module xor_circuit_with_3_input (
  input  in_1,
  input  in_2,
  input  in_3,
  output out_4
);

  ExactlyOne xor_1 (.out(out_4), .in0(in_1), .in1(in_2), .in2(in_3));
endmodule

module compartment (
  input  in_1,
  output out_2
);

  buf buffer_1 (out_2, in_1);
endmodule

module colling_system (
  input  in_1,
  input  in_2,
  output out_3
);

  and and_1 (out_3, in_1, in_2);
endmodule
