// Logisim project project.circ as structural Verilog: 1 circuit, main circuit main
module main (
  input  X,
  input  Y,
  input  Z,
  output a,
  output b,
  output C,
  output d,
  output e,
  output f,
  output g
);

  wire and_1_out, and_2_out, and_3_out, and_4_out, and_5_out, and_6_out, and_7_out, and_8_out, and_9_out,
       not_1_out, not_2_out, not_3_out;

  not not_1 (not_1_out, X);
  not not_2 (not_2_out, Y);
  not not_3 (not_3_out, Z);
  and and_1 (and_1_out, not_2_out, Z);
  and and_2 (and_2_out, X, Y, not_3_out);
  and and_3 (and_3_out, not_1_out, not_3_out);
  and and_4 (and_4_out, X, Z);
  and and_5 (and_5_out, Y, not_3_out);
  and and_6 (and_6_out, X, not_2_out);
  and and_7 (and_7_out, not_1_out, Y, not_3_out);
  and and_8 (and_8_out, X, Y);
  and and_9 (and_9_out, not_1_out, not_2_out, Z);
  or or_1 (a, and_1_out, and_2_out);
  or or_2 (b, and_3_out, Y, and_4_out);
  or or_3 (C, not_1_out, Y, Z);
  or or_4 (d, and_1_out, and_5_out, X);
  or or_5 (e, and_1_out, and_6_out, and_7_out);
  or or_6 (f, and_6_out, and_1_out);
  or or_7 (g, and_8_out, and_9_out);
  _7_Segment_Display u_7_segment_display_1 (.g(g), .f(f), .a(a), .b(b), .e(e), .d(d), .c(C));  // open: dp

  // Notes on the sheet:
  //   YZ'
  //   XY'
  //   Y'Z
  //   XYZ'
  //   X'Z'
  //   XZ
endmodule
