// Logisim project XNOR using nand gate.circ as structural Verilog
module NOR_gate (
  input  in_1,
  input  in_2,
  output out_3
);

  nor nor_1 (out_3, in_1, in_2);
endmodule

module Nand_gate (
  input  in_1,
  input  in_2,
  output out_3
);

  nand nand_1 (out_3, in_1, in_2);
endmodule

module XOR_using_nand (
  input  A,
  input  B,
  output out_3
);

  wire nand_1_out, nand_2_out, nand_3_out;

  nand nand_1 (nand_1_out, A, B);
  nand nand_2 (nand_2_out, A, nand_1_out);
  nand nand_3 (nand_3_out, nand_1_out, B);
  nand nand_4 (out_3, nand_2_out, nand_3_out);
endmodule

module XOR_using_nor (
  input  A,
  input  B,
  output out_3
);

  wire nor_1_out, nor_2_out, nor_3_out, nor_4_out;

  nor nor_1 (nor_1_out, A, A);
  nor nor_2 (nor_2_out, B, B);
  nor nor_3 (nor_3_out, A, B);
  nor nor_4 (nor_4_out, nor_1_out, nor_2_out);
  nor nor_5 (out_3, nor_4_out, nor_3_out);
endmodule

module XNOR_using_Nand (
  input  A,
  input  B,
  output out_3
);

  wire nand_1_out, nand_2_out, nand_3_out, nand_4_out;

  nand nand_1 (nand_1_out, A, B);
  nand nand_2 (nand_2_out, A, nand_1_out);
  nand nand_3 (nand_3_out, nand_1_out, B);
  nand nand_4 (nand_4_out, nand_2_out, nand_3_out);
  nand nand_5 (out_3, nand_4_out, nand_4_out);
endmodule

module XNOR_using_Nor (
  input  A,
  input  B,
  output out_3
);

  wire nor_1_out, nor_2_out, nor_3_out;

  nor nor_1 (nor_1_out, A, B);
  nor nor_2 (nor_2_out, A, nor_1_out);
  nor nor_3 (nor_3_out, nor_1_out, B);
  nor nor_4 (out_3, nor_2_out, nor_3_out);
endmodule

module f_with_nans (
  input  A,
  input  B,
  input  C,
  output out_4
);

  wire nand_gate_1_out_3, nand_gate_2_out_3, not_1_out;

  not not_1 (not_1_out, C);
  Nand_gate nand_gate_1 (.in_1(A), .in_2(C), .out_3(nand_gate_1_out_3));
  Nand_gate nand_gate_2 (.in_1(B), .in_2(not_1_out), .out_3(nand_gate_2_out_3));
  Nand_gate nand_gate_3 (.in_1(nand_gate_1_out_3), .in_2(nand_gate_2_out_3), .out_3(out_4));
endmodule

module f_using_nor (
  input  A,
  input  B,
  input  C,
  output out_4
);

  NOR_gate nor_gate_1 (.in_1(A), .in_2(C), .out_3(out_4));
endmodule
