// Logisim project 7411 ic.circ as structural Verilog
module _7411ic (
  input  in_1,
  input  in_2,
  input  in_3,
  input  in_4,
  input  in_5,
  input  in_6,
  input  in_7,
  input  in_8,
  input  in_9,
  output out_10,
  output out_11,
  output out_12
);

  and and_1 (out_10, in_1, in_2, in_3);
  and and_2 (out_11, in_4, in_5, in_6);
  and and_3 (out_12, in_7, in_8, in_9);
endmodule

module _4075ic (
  input  in_1,
  input  in_2,
  input  in_3,
  input  in_4,
  input  in_5,
  input  in_6,
  input  in_7,
  input  in_8,
  input  in_9,
  output out_10,
  output out_11,
  output out_12
);

  or or_1 (out_10, in_1, in_2, in_3);
  or or_2 (out_11, in_4, in_5, in_6);
  or or_3 (out_12, in_7, in_8, in_9);
endmodule

module _7404_ic (
  input  in_1,
  input  in_2,
  input  in_3,
  input  in_4,
  input  in_5,
  input  in_6,
  output out_7,
  output out_8,
  output out_9,
  output out_10,
  output out_11,
  output out_12
);

  not not_1 (out_7, in_1);
  not not_2 (out_8, in_2);
  not not_3 (out_9, in_3);
  not not_4 (out_10, in_4);
  not not_5 (out_11, in_5);
  not not_6 (out_12, in_6);
endmodule

module _1st_canonial_form (
  input  A,
  input  B,
  input  C,
  output F
);

  wire n7411ic_1_out_10, n7411ic_1_out_11, n7411ic_1_out_12, not_1_out, not_2_out, not_3_out;

  not not_1 (not_1_out, A);
  not not_2 (not_2_out, B);
  not not_3 (not_3_out, C);
  _7411ic u_7411ic_1 (
    .in_1(not_1_out), .in_2(not_2_out), .in_3(C), .out_10(n7411ic_1_out_10), .in_4(not_1_out), .in_5(B),
    .out_11(n7411ic_1_out_11), .in_6(not_3_out), .in_7(A), .in_8(B), .out_12(n7411ic_1_out_12),
    .in_9(not_3_out));
  _4075ic u_4075ic_1 (
    .in_4(n7411ic_1_out_10), .in_5(n7411ic_1_out_11), .in_6(n7411ic_1_out_12), .out_11(F));  // open: in_1, in_2, in_3, in_7, in_8, in_9, out_10, out_12
endmodule

module _2nd_canonical_form (
  input  A,
  input  B,
  input  C,
  output F
);

  wire n4075ic_1_out_10, n4075ic_1_out_11, n4075ic_1_out_12, n4075ic_2_out_11, n4075ic_2_out_12,
       n7411ic_1_out_11, not_1_out, not_2_out, not_3_out;

  not not_1 (not_1_out, A);
  not not_2 (not_2_out, B);
  not not_3 (not_3_out, C);
  _4075ic u_4075ic_1 (
    .in_1(A), .in_2(B), .in_3(C), .in_4(A), .in_5(not_2_out), .in_6(not_3_out), .in_7(not_1_out),
    .in_8(not_2_out), .in_9(not_3_out), .out_10(n4075ic_1_out_10), .out_11(n4075ic_1_out_11),
    .out_12(n4075ic_1_out_12));
  _4075ic u_4075ic_2 (
    .in_4(not_1_out), .in_5(B), .in_6(not_3_out), .in_7(not_1_out), .in_8(not_2_out), .in_9(not_3_out),
    .out_11(n4075ic_2_out_11), .out_12(n4075ic_2_out_12));  // open: in_1, in_2, in_3, out_10
  _7411ic u_7411ic_1 (
    .in_4(n4075ic_2_out_12), .in_5(n4075ic_2_out_11), .out_11(n7411ic_1_out_11), .in_6(n4075ic_1_out_12),
    .in_7(n7411ic_1_out_11), .in_8(n4075ic_1_out_10), .out_12(F), .in_9(n4075ic_1_out_11));  // open: in_1, in_2, in_3, out_10
endmodule
