// Logisim project LAB6.circ as structural Verilog: 1 circuit, main circuit main
module main (
  input  A,
  input  B,
  input  C,
  input  D,
  output a_2,
  output b_2,
  output c_2,
  output d_2,
  output e,
  output f,
  output g
);

  wire and_1_out, and_2_out, and_3_out, and_4_out, and_5_out, and_6_out, and_7_out, and_8_out, and_9_out,
       not_1_out, not_2_out, not_3_out, not_4_out;

  not not_1 (not_1_out, A);
  not not_2 (not_2_out, B);
  not not_3 (not_3_out, C);
  not not_4 (not_4_out, D);
  and and_1 (and_1_out, B, not_3_out);
  and and_2 (and_2_out, B, not_4_out);
  and and_3 (and_3_out, B, D);
  and and_4 (and_4_out, not_2_out, not_4_out);
  and and_5 (and_5_out, C, D);
  and and_6 (and_6_out, not_3_out, not_4_out);
  or or_1 (c_2, B, not_3_out, D);
  and and_7 (and_7_out, C, not_4_out);
  and and_8 (and_8_out, not_2_out, C);
  and and_9 (and_9_out, D, and_1_out);
  or or_2 (a_2, and_3_out, and_4_out, C, A);
  or or_3 (b_2, and_5_out, not_2_out, and_6_out);
  or or_4 (d_2, and_4_out, A, and_7_out, and_8_out, and_9_out);
  or or_5 (e, and_7_out, and_4_out);
  or or_6 (f, A, and_2_out, and_1_out, A);
  or or_7 (g, and_7_out, and_1_out, A, and_8_out);
  _7_Segment_Display u_7_segment_display_1 (.g(g), .f(f), .a(a_2), .b(b_2), .e(e), .d(d_2), .c(c_2));  // open: dp

  // Notes on the sheet:
  //   BC`
  //   BD`
  //   BD
  //   B`D`
  //   CD
  //   C`D`
  //   CD`
  //   B`C
  //   BC`D
endmodule
