// Logisim project lab8.circ as structural Verilog: 1 circuit, main circuit main
module main (
  input  in_1,
  input  in_2,
  output out_3,
  output out_4
);

  wire clock_1_out, d_ff_1_qn, undriven;

  Clock clock_1 (.out(clock_1_out));
  D_Flip_Flop d_ff_1 (
    .clk(clock_1_out), .D(in_1), .Q(out_3), .Qn(d_ff_1_qn), .preset(undriven), .reset(in_2));  // open: en
  D_Flip_Flop d_ff_2 (.clk(clock_1_out), .D(d_ff_1_qn), .Q(out_4), .reset(in_2));  // open: Qn, preset, en
endmodule
